# Fritzing sketch CleanAirFrome_pcb_d1_mini_pro_ADS1115 (saved by Fritzing 0.9.3b)
circuit board: 6.50001cm x 6.99729cm

parts:
  R1 = Resistor [tolerance=±5% resistance=4.7k package=THT]
  J8 = Generic male header - 4 pins [form="♂ (male)" part_number=I2C-5-1 package=THT]
  J4 = Generic male header - 4 pins [form="♂ (male)" part_number=I2C-3-3 package=THT]
  J3 = Generic male header - 4 pins [form="♂ (male)" part_number=I2C-3-1 package=THT]
  J2 = Generic male header - 4 pins [form="♂ (male)" part_number=I2C-3-2 package=THT]
  J7 = Generic male header - 4 pins [form="♂ (male)" part_number=I2C-5-2 package=THT]
  J5 = Generic male header - 4 pins [form="♂ (male)" part_number=I2C-3-4 package=THT]
  J6 = Generic male header - 4 pins [form="♂ (male)" part_number=I2C-3-5 package=THT]
  J9 = Generic male header - 4 pins [form="♂ (male)" part_number=DHT22 package=THT]
  D1_Mini_Pro = WeMos D1 Mini
  SDS011 = Generic male header - 5 pins [form="♂ (male)" package=THT]
  J10 = Generic male header - 4 pins [form="♂ (male)" package=THT]
  ADS1115 = Adafruit ADS1115 16Bit I2C ADC [part_number="Adafruit #1085"]

nets:
  N1: R1.Pin_0, J9.pin3, D1_Mini_Pro.D7
  3V3: R1.Pin_1, J4.pin1, J3.pin1, J2.pin1, J5.pin1, J6.pin1, J9.pin4, D1_Mini_Pro.3V3, ADS1115.VDD
  N2: J8.pin1, J7.pin1, D1_Mini_Pro.5V, SDS011.pin2
  GND: J8.gnd, J4.gnd, J3.gnd, J2.gnd, J7.gnd, J5.gnd, J6.gnd, J9.pin1, D1_Mini_Pro.G, SDS011.pin3, ADS1115.GND
  N3: J8.pin3, J4.pin3, J3.pin3, J2.pin3, J7.pin3, J5.pin3, J6.pin3, D1_Mini_Pro.D4, ADS1115.SCL
  N4: J8.pin4, J4.pin4, J3.pin4, J2.pin4, J7.pin4, J5.pin4, J6.pin4, D1_Mini_Pro.D3, ADS1115.SDA
  N5: D1_Mini_Pro.D1, SDS011.pin5
  N6: D1_Mini_Pro.D2, SDS011.pin4
  N7: J10.pin1, ADS1115.AIN0
  N8: J10.pin2, ADS1115.AIN1
  N9: J10.pin3, ADS1115.AIN2
  N10: J10.pin4, ADS1115.AIN3

notes:
  SDA
  SCL
  GND
  VCC
  VCC5V
  TX
  RX
  VCC 5V
  VCC3.3V
  DAT
  CleanAirFrome
  A0
  A1
  A2
  A3

custom parts:
  Generic male header - 4 pins: Generic male header
  Generic male header - 4 pins: Generic male header
  WeMos D1 Mini: The D1 mini is a mini wifi board based on ESP-8266EX.
  Generic male header - 5 pins: Generic male header
  Adafruit ADS1115 16Bit I2C ADC: For microcontrollers without an analog-to-digital converter or when you want a higher-precision ADC, the ADS1115 provides 16-bit precision at 860 samples/second over I2C. The chip can be configured as 4 single-ended input channels, or two differential channels. As a nice bonus, it even includes a programmable gain amplifier, up to x16, to help boost up smaller single/differential signals to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
